# Fritzing sketch sonotify (saved by Fritzing 1.0.7)

parts:
  M1 = DOIT Esp32 DevKit v1 (30 pins long, 11 pins width) [part_number=ESP32S-PIN30]
  LED1 = smd LED [color="Red (633nm)" package="0805 [SMD]"]
  R1 = Resistor [tolerance=±5% power=0.25W resistance=220 package=THT]
  Part2 = RFID-RC522-v3

nets:
  3V3: M1.3V3, Part2.3.3V
  GND: M1.GND, LED1.cathode, Part2.GND
  N1: M1.D19, Part2.SCK
  N2: M1.D21, Part2.RST
  N3: M1.D22, Part2.SDA
  N4: M1.D23, Part2.MOSI
  N5: M1.D32, R1.Pin_0
  N6: M1.D25, Part2.MISO
  N7: LED1.anode, R1.Pin_1

custom parts:
  DOIT Esp32 DevKit v1 (30 pins long, 11 pins width): The DOIT Esp32 DevKit v1 is one of the development board created by DOIT to evaluate the ESP-WROOM-32 module. It is based on the ESP32 microcontroller that boasts Wifi, Bluetooth, Ethernet and Low Power support all in a single chip. (vanepp) made breadboard work, adjusted pin numbering and labels and reduced size of schematic and cleaned up pcb. This chip is 30pins long (2 x15) and 11 pins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
  RFID-RC522-v3: A simple China made RFID-RC522 Reader (6x4 cm); do check the pin labels, as this is a MFRC522 based clone.
